# Fritzing sketch TheInstrument (saved by Fritzing 0.9.3b)
breadboards: 1

parts:
  Part1 = Arduino Mega 2560 (Rev3)
  HC-SR04_Sensor_1 = HC-SR04 Ultrasonic Distance Sensor
  J1 = Piezo Speaker
  Q1 = NPN-Transistor [package="TO92 [THT]"]
  R1 = Resistor [tolerance=±5% resistance=220 package=THT]
  LED1 = RGB LED (com. cathode, rgb) [package="5 mm [THT]"]
  R2 = Resistor [tolerance=±5% resistance=220 package=THT]
  R3 = Resistor [tolerance=±5% resistance=220 package=THT]
  R4 = Resistor [tolerance=±5% resistance=220 package=THT]

nets:
  5V: Part1.5V, HC-SR04_Sensor_1.VCC, J1.pin2, LED1.green_anode
  GND: Part1.GND, HC-SR04_Sensor_1.GND, Q1.E
  N1: Part1.D22, R1.Pin_1
  N2: Part1.D23, R2.Pin_0
  N3: Part1.D24, R3.Pin_0
  N4: Part1.D25, R4.Pin_0
  N5: Part1.D52, HC-SR04_Sensor_1.TRIG
  N6: Part1.D53, HC-SR04_Sensor_1.ECHO
  N7: J1.pin1, Q1.C
  N8: Q1.B, R1.Pin_0
  N9: LED1.red_anode, R2.Pin_1
  N10: LED1.common_cathode, R3.Pin_1
  N11: LED1.blue_anode, R4.Pin_1
